// Logisim project CPU.circ as structural Verilog: 6 circuits, main circuit main
module main (
);

  ALU alu_1 ();  // open: enable_del_dmx, in1, in2, in3, in4, in5, in6, in7, in8, opcode_1, opcode_2, opcode3, opcode_4, Overflow, Overflow_2, out_1, out_2, out_3, out_4
endmodule

module ALU (
  input  enable_del_dmx,
  input  opcode_1,
  input  opcode_2,
  input  opcode3,
  input  opcode_4,
  input  in1,
  input  in2,
  input  in3,
  input  in4,
  input  in5,
  input  in6,
  input  in7,
  input  in8,
  output out_1,
  output out_2,
  output out_3,
  output out_4,
  output Overflow,
  output Overflow_2
);

  wire add_1_out_10, add_1_out_11, add_1_out_12, add_1_out_13, and_1_out, and_2_out, and_3_out, and_4_out,
       demultiplexer_1_out1, demultiplexer_1_out2, demultiplexer_1_out3, demultiplexer_1_out4,
       demultiplexer_1_out5, demultiplexer_1_out6, not_1_out, or_1_out, or_2_out, or_3_out, or_4_out,
       reloj_out, subs_1_out_10, subs_1_out_11, subs_1_out_12, subs_1_out_13, xor_1_out, xor_2_out,
       xor_3_out, xor_4_out;

  assign out_1 = demultiplexer_1_out1 ? and_1_out : 1'bz;  // Controlled_Buffer controlled_buffer_1
  and and_1 (and_1_out, in1, in5);
  assign out_2 = demultiplexer_1_out1 ? and_2_out : 1'bz;  // Controlled_Buffer controlled_buffer_2
  and and_2 (and_2_out, in2, in6);
  assign out_3 = demultiplexer_1_out1 ? and_3_out : 1'bz;  // Controlled_Buffer controlled_buffer_3
  and and_3 (and_3_out, in3, in7);
  assign out_4 = demultiplexer_1_out1 ? and_4_out : 1'bz;  // Controlled_Buffer controlled_buffer_4
  and and_4 (and_4_out, in4, in8);
  assign out_1 = demultiplexer_1_out2 ? or_1_out : 1'bz;  // Controlled_Buffer controlled_buffer_5
  or or_1 (or_1_out, in1, in5);
  or or_2 (or_2_out, in2, in6);
  assign out_2 = demultiplexer_1_out2 ? or_2_out : 1'bz;  // Controlled_Buffer controlled_buffer_6
  assign out_3 = demultiplexer_1_out2 ? or_3_out : 1'bz;  // Controlled_Buffer controlled_buffer_7
  or or_3 (or_3_out, in3, in7);
  or or_4 (or_4_out, in4, in8);
  assign out_4 = demultiplexer_1_out2 ? or_4_out : 1'bz;  // Controlled_Buffer controlled_buffer_8
  assign out_1 = demultiplexer_1_out3 ? xor_1_out : 1'bz;  // Controlled_Buffer controlled_buffer_9
  xor xor_1 (xor_1_out, in1, in5);
  xor xor_2 (xor_2_out, in2, in6);
  assign out_2 = demultiplexer_1_out3 ? xor_2_out : 1'bz;  // Controlled_Buffer controlled_buffer_10
  assign out_3 = demultiplexer_1_out3 ? xor_3_out : 1'bz;  // Controlled_Buffer controlled_buffer_11
  xor xor_3 (xor_3_out, in3, in7);
  xor xor_4 (xor_4_out, in4, in8);
  assign out_1 = demultiplexer_1_out4 ? ~in1 : 1'bz;  // Controlled_Inverter controlled_inverter_1
  assign out_2 = demultiplexer_1_out4 ? ~in2 : 1'bz;  // Controlled_Inverter controlled_inverter_2
  assign out_3 = demultiplexer_1_out4 ? ~in3 : 1'bz;  // Controlled_Inverter controlled_inverter_3
  not not_1 (not_1_out, demultiplexer_1_out5);
  assign out_4 = demultiplexer_1_out5 ? add_1_out_10 : 1'bz;  // Controlled_Buffer controlled_buffer_12
  assign out_3 = demultiplexer_1_out5 ? add_1_out_11 : 1'bz;  // Controlled_Buffer controlled_buffer_13
  ADD add_1 (
    .A0(in4), .A1(in3), .A2(in2), .A3(in1), .B0(in8), .B1(in7), .B2(in6), .B3(in5), .in_1(not_1_out),
    .Overflow(Overflow), .out_10(add_1_out_10), .out_11(add_1_out_11), .out_12(add_1_out_12),
    .out_13(add_1_out_13));
  assign out_2 = demultiplexer_1_out5 ? add_1_out_12 : 1'bz;  // Controlled_Buffer controlled_buffer_14
  assign out_4 = demultiplexer_1_out6 ? subs_1_out_10 : 1'bz;  // Controlled_Buffer controlled_buffer_15
  SUBS subs_1 (
    .A0(in4), .A1(in3), .A2(in2), .A3(in1), .B0(in8), .B1(in7), .B2(in6), .B3(in5),
    .in_2(demultiplexer_1_out6), .Overflow(Overflow_2), .out_10(subs_1_out_10), .out_11(subs_1_out_11),
    .out_12(subs_1_out_12), .out_13(subs_1_out_13));
  assign out_3 = demultiplexer_1_out6 ? subs_1_out_11 : 1'bz;  // Controlled_Buffer controlled_buffer_16
  assign out_2 = demultiplexer_1_out6 ? subs_1_out_12 : 1'bz;  // Controlled_Buffer controlled_buffer_17
  Clock reloj (.out(reloj_out));
  Demultiplexer #(.select(4)) demultiplexer_1 (
    .out1(demultiplexer_1_out1), .out2(demultiplexer_1_out2), .out3(demultiplexer_1_out3),
    .out4(demultiplexer_1_out4), .out5(demultiplexer_1_out5), .out6(demultiplexer_1_out6), .in(reloj_out),
    .sel({opcode_1, opcode_2, opcode3, opcode_4}), .en(enable_del_dmx));  // open: out0, out7, out8, out9, out10, out11, out12, out13, out14, out15
  assign out_4 = demultiplexer_1_out3 ? xor_4_out : 1'bz;  // Controlled_Buffer controlled_buffer_18
  assign out_4 = demultiplexer_1_out4 ? ~in4 : 1'bz;  // Controlled_Inverter controlled_inverter_4
  assign out_1 = demultiplexer_1_out5 ? add_1_out_13 : 1'bz;  // Controlled_Buffer controlled_buffer_19
  assign out_1 = demultiplexer_1_out6 ? subs_1_out_13 : 1'bz;  // Controlled_Buffer controlled_buffer_20
endmodule

module ADD (
  input  in_1,
  input  A0,
  input  A1,
  input  A2,
  input  A3,
  input  B0,
  input  B1,
  input  B2,
  input  B3,
  output out_10,
  output out_11,
  output out_12,
  output out_13,
  output Overflow
);

  wire n1_bit_adder_1_c_out, n1_bit_adder_2_c_out, n1_bit_adder_3_c_out;

  _1_bit_adder u_1_bit_adder_1 (.A(A0), .B(B0), .C_in(in_1), .C_out(n1_bit_adder_1_c_out), .Sum(out_10));
  _1_bit_adder u_1_bit_adder_2 (
    .A(A1), .B(B1), .C_in(n1_bit_adder_1_c_out), .C_out(n1_bit_adder_2_c_out), .Sum(out_11));
  _1_bit_adder u_1_bit_adder_3 (
    .A(A2), .B(B2), .C_in(n1_bit_adder_2_c_out), .C_out(n1_bit_adder_3_c_out), .Sum(out_12));
  _1_bit_adder u_1_bit_adder_4 (.A(A3), .B(B3), .C_in(n1_bit_adder_3_c_out), .C_out(Overflow), .Sum(out_13));
endmodule

module _1_bit_adder (
  input  C_in,
  input  A,
  input  B,
  output Sum,
  output C_out
);

  wire and_1_out, and_2_out, and_3_out, xor_2_out;

  and and_1 (and_1_out, C_in, A);
  and and_2 (and_2_out, C_in, B);
  and and_3 (and_3_out, A, B);
  xor xor_1 (Sum, C_in, xor_2_out);
  xor xor_2 (xor_2_out, A, B);
  or or_1 (C_out, and_1_out, and_2_out, and_3_out);
endmodule

module SUBS (
  input  A0,
  input  in_2,
  input  A1,
  input  A2,
  input  A3,
  input  B0,
  input  B1,
  input  B2,
  input  B3,
  output out_10,
  output out_11,
  output out_12,
  output out_13,
  output Overflow
);

  wire n1_bit_adder_1_c_out, n1_bit_adder_2_c_out, n1_bit_adder_3_c_out, not_1_out, not_2_out, not_3_out,
       not_4_out;

  not not_1 (not_1_out, B2);
  not not_2 (not_2_out, B0);
  not not_3 (not_3_out, B1);
  not not_4 (not_4_out, B3);
  _1_bit_adder u_1_bit_adder_1 (.A(A0), .B(not_2_out), .C_in(in_2), .C_out(n1_bit_adder_1_c_out), .Sum(out_10));
  _1_bit_adder u_1_bit_adder_2 (
    .A(A1), .B(not_3_out), .C_in(n1_bit_adder_1_c_out), .C_out(n1_bit_adder_2_c_out), .Sum(out_11));
  _1_bit_adder u_1_bit_adder_3 (
    .A(A2), .B(not_1_out), .C_in(n1_bit_adder_2_c_out), .C_out(n1_bit_adder_3_c_out), .Sum(out_12));
  _1_bit_adder u_1_bit_adder_4 (.A(A3), .B(not_4_out), .C_in(n1_bit_adder_3_c_out), .C_out(Overflow), .Sum(out_13));
endmodule

module REGISTROS (
  input  in_1,
  input  in_2,
  input  in_3,
  input  in_4,
  input  in_5,
  input  in_6,
  input  in_7,
  input  in_8,
  input  in_9,
  input  in_10,
  input  in_11,
  output out_12,
  output out_13,
  output out_14,
  output out_15,
  output out_16,
  output out_17,
  output out_18,
  output out_19
);

  wire clock_1_out, demultiplexer_1_out0, demultiplexer_1_out1, demultiplexer_1_out2, demultiplexer_1_out3,
       register_1_q, register_2_q, register_3_q, register_4_q, register_5_q, register_6_q, register_7_q,
       register_8_q, register_9_q, register_10_q, register_11_q, register_12_q, register_13_q, register_14_q,
       register_15_q, register_16_q, undriven;

  Clock clock_1 (.out(clock_1_out));
  Demultiplexer #(.select(2)) demultiplexer_1 (
    .out0(demultiplexer_1_out0), .out1(demultiplexer_1_out1), .out2(demultiplexer_1_out2),
    .out3(demultiplexer_1_out3), .in(clock_1_out), .sel({in_5, in_6}), .en(in_7));
  Register #(.width(1)) register_1 (.D(in_8), .Q(register_1_q), .clk(demultiplexer_1_out0));  // open: en, clr
  Register #(.width(1)) register_2 (.D(in_9), .Q(register_2_q), .clk(demultiplexer_1_out0));  // open: en, clr
  Register #(.width(1)) register_3 (.D(in_10), .Q(register_3_q), .clk(demultiplexer_1_out0));  // open: en, clr
  Register #(.width(1)) register_4 (.D(in_11), .Q(register_4_q), .clk(demultiplexer_1_out0));  // open: en, clr
  Register #(.width(1)) register_5 (.D(in_8), .Q(register_5_q), .clk(demultiplexer_1_out1));  // open: en, clr
  Register #(.width(1)) register_6 (.D(in_9), .Q(register_6_q), .clk(demultiplexer_1_out1));  // open: en, clr
  Register #(.width(1)) register_7 (.D(in_10), .Q(register_7_q), .clk(demultiplexer_1_out1));  // open: en, clr
  Register #(.width(1)) register_8 (.D(in_11), .Q(register_8_q), .clk(demultiplexer_1_out1));  // open: en, clr
  Register #(.width(1)) register_9 (.D(in_8), .Q(register_9_q), .clk(demultiplexer_1_out2));  // open: en, clr
  Register #(.width(1)) register_10 (.D(in_9), .Q(register_10_q), .clk(demultiplexer_1_out2));  // open: en, clr
  Register #(.width(1)) register_11 (.D(in_10), .Q(register_11_q), .clk(demultiplexer_1_out2));  // open: en, clr
  Register #(.width(1)) register_12 (.D(in_11), .Q(register_12_q), .clk(demultiplexer_1_out2));  // open: en, clr
  Register #(.width(1)) register_13 (.D(in_8), .Q(register_13_q), .clk(demultiplexer_1_out3));  // open: en, clr
  Register #(.width(1)) register_14 (.D(in_9), .Q(register_14_q), .clk(demultiplexer_1_out3));  // open: en, clr
  Register #(.width(1)) register_15 (.D(in_10), .Q(register_15_q), .clk(demultiplexer_1_out3));  // open: en, clr
  Register #(.width(1)) register_16 (.D(in_11), .Q(register_16_q), .clk(demultiplexer_1_out3));  // open: en, clr
  Multiplexer #(.select(2)) multiplexer_1 (
    .in0(register_1_q), .in1(register_5_q), .in2(register_9_q), .in3(register_13_q), .out(out_12),
    .sel({in_1, in_2}), .en(undriven));
  Multiplexer #(.select(2)) multiplexer_2 (
    .in0(register_2_q), .in1(register_6_q), .in2(register_10_q), .in3(register_14_q), .out(out_13),
    .sel({in_1, in_2}), .en(undriven));
  Multiplexer #(.select(2)) multiplexer_3 (
    .in0(register_3_q), .in1(register_7_q), .in2(register_11_q), .in3(register_15_q), .out(out_14),
    .sel({in_1, in_2}), .en(undriven));
  Multiplexer #(.select(2)) multiplexer_4 (
    .in0(register_4_q), .in1(register_8_q), .in2(register_12_q), .in3(register_16_q), .out(out_15),
    .sel({in_1, in_2}), .en(undriven));
  Multiplexer #(.select(2)) multiplexer_5 (
    .in0(register_1_q), .in1(register_5_q), .in2(register_9_q), .in3(register_13_q), .out(out_16),
    .sel({in_3, in_4}), .en(undriven));
  Multiplexer #(.select(2)) multiplexer_6 (
    .in0(register_2_q), .in1(register_6_q), .in2(register_10_q), .in3(register_14_q), .out(out_17),
    .sel({in_3, in_4}), .en(undriven));
  Multiplexer #(.select(2)) multiplexer_7 (
    .in0(register_3_q), .in1(register_7_q), .in2(register_11_q), .in3(register_15_q), .out(out_18),
    .sel({in_3, in_4}), .en(undriven));
  Multiplexer #(.select(2)) multiplexer_8 (
    .in0(register_4_q), .in1(register_8_q), .in2(register_12_q), .in3(register_16_q), .out(out_19),
    .sel({in_3, in_4}), .en(undriven));
endmodule
